# Fritzing sketch meteo (saved by Fritzing 0.9.3b)
breadboards: 1

parts:
  WeMos_D1_Mini1 = WeMos D1 Mini
  Part1 = Barometric Pressure Sensor - BMP180 Breakout (GY-68)
  DS1 = DS18B20 1-Wire Temperature Sensor [part_number=DS18B20]
  R1 = Resistor [tolerance=±5% resistance=4.7k package=THT]
  RHT1 = Humidity and Temperature Sensor RHT03
  R2 = Resistor [tolerance=±5% resistance=4.7k package=THT]
  R3 = Resistor [tolerance=±5% resistance=1k package=THT]
  LED1 = smd LED [color="Red (633nm)" package="1206 [SMD]"]

nets:
  5V: WeMos_D1_Mini1.5V, Part1.VCC, DS1.VDD, R1.Pin_1, RHT1.Vcc, R2.Pin_0
  N1: WeMos_D1_Mini1.D0, R3.Pin_0
  N2: WeMos_D1_Mini1.D1, Part1.SCL
  N3: WeMos_D1_Mini1.D2, Part1.SDA
  N4: WeMos_D1_Mini1.D4, DS1.DQ
  N5: WeMos_D1_Mini1.D7, RHT1.Data-signal
  GND: WeMos_D1_Mini1.G, Part1.GND, DS1.GND, RHT1.GND_1, LED1.cathode
  N6: R3.Pin_1, LED1.anode
